# Fritzing sketch EQMODWiFi (saved by Fritzing 0.9.3b)
circuit board: 8.46667cm x 5.64444cm
breadboards: 1

parts:
  WeMos_D1_Mini1 = WeMos D1 Mini
  C1 = Capacitor Polarized [part_number="10uF 25V" package=cpol-radial-100uf-25v]
  C2 = Capacitor Polarized [part_number="10uF 10V" package=cpol-radial-100uf-25v]
  C3 = Capacitor [part_number=u1 package=cap-pth-small-kit]
  C4 = Capacitor [part_number=u1 package=cap-pth-small-kit]
  JP1 = Header 4 [package=molex-1x4_lock]
  U2 = Voltage Regulator - 5V [package="DPak [SMD]"]
  R2 = Resistor [tolerance=±5% resistance=3.3k package=THT]
  R1 = Resistor [tolerance=±5% resistance=6.8k package=THT]

nets:
  N1: WeMos_D1_Mini1.5V, C2.+, C3.1, U2.output_voltage
  N2: WeMos_D1_Mini1.D7, R2.Pin_0, R1.Pin_1
  N3: WeMos_D1_Mini1.D8, JP1.3
  N4: WeMos_D1_Mini1.G, C1.-, C2.-, C3.2, C4.2, JP1.4, U2.GND, R1.Pin_0
  N5: C1.+, C4.1, JP1.1, U2.input_voltage
  N6: JP1.2, R2.Pin_1

notes:
  1. DB9 - 1 - 12V
  2. DB9 - 9 - TxD
  3. DB9 - 6 - RxD
  4. DB9 - 5 - GND

custom parts:
  WeMos D1 Mini: The D1 mini is a mini wifi board based on ESP-8266EX.
